// Logisim project EP1.circ as structural Verilog: 5 circuits, main circuit main
module main (
  input  A0,
  input  A1,
  input  Cin,
  input  A2,
  input  A3,
  input  B0,
  input  B1,
  input  B2,
  input  B3,
  output S0,
  output S1,
  output S2,
  output S3,
  output Cout,
  output Overflow
);

  wire decod_hexa_1_a, decod_hexa_1_b, decod_hexa_1_c, decod_hexa_1_d, decod_hexa_1_dp, decod_hexa_1_e,
       decod_hexa_1_f, decod_hexa_1_g, decod_hexa_2_a, decod_hexa_2_b, decod_hexa_2_c, decod_hexa_2_d,
       decod_hexa_2_dp, decod_hexa_2_e, decod_hexa_2_f, decod_hexa_2_g, decod_hexa_3_a, decod_hexa_3_b,
       decod_hexa_3_c, decod_hexa_3_d, decod_hexa_3_dp, decod_hexa_3_e, decod_hexa_3_f, decod_hexa_3_g;

  decod_hexa decod_hexa_1 (
    .E3(A3), .E2(A2), .E1(A1), .E0(A0), .A(decod_hexa_1_a), .B(decod_hexa_1_b), .C(decod_hexa_1_c),
    .D(decod_hexa_1_d), .E(decod_hexa_1_e), .F(decod_hexa_1_f), .G(decod_hexa_1_g), .DP(decod_hexa_1_dp));
  somador_4bits somador_4bits_1 (
    .A0(A0), .A1(A1), .A2(A2), .A3(A3), .B0(B0), .B1(B1), .B2(B2), .B3(B3), .Cin(Cin), .Cout(Cout), .S0(S0),
    .S1(S1), .S2(S2), .S3(S3), .Overflow(Overflow));
  decod_hexa decod_hexa_2 (
    .E3(B3), .E2(B2), .E1(B1), .E0(B0), .A(decod_hexa_2_a), .B(decod_hexa_2_b), .C(decod_hexa_2_c),
    .D(decod_hexa_2_d), .E(decod_hexa_2_e), .F(decod_hexa_2_f), .G(decod_hexa_2_g), .DP(decod_hexa_2_dp));
  _7_Segment_Display u_7_segment_display_1 (
    .g(decod_hexa_1_f), .f(decod_hexa_1_g), .a(decod_hexa_1_a), .b(decod_hexa_1_b), .e(decod_hexa_1_e),
    .d(decod_hexa_1_d), .c(decod_hexa_1_c), .dp(decod_hexa_1_dp));
  _7_Segment_Display u_7_segment_display_2 (
    .g(decod_hexa_2_f), .f(decod_hexa_2_g), .a(decod_hexa_2_a), .b(decod_hexa_2_b), .e(decod_hexa_2_e),
    .d(decod_hexa_2_d), .c(decod_hexa_2_c), .dp(decod_hexa_2_dp));
  decod_hexa decod_hexa_3 (
    .E3(S3), .E2(S2), .E1(S1), .E0(S0), .A(decod_hexa_3_a), .B(decod_hexa_3_b), .C(decod_hexa_3_c),
    .D(decod_hexa_3_d), .E(decod_hexa_3_e), .F(decod_hexa_3_f), .G(decod_hexa_3_g), .DP(decod_hexa_3_dp));
  _7_Segment_Display u_7_segment_display_3 (
    .g(decod_hexa_3_f), .f(decod_hexa_3_g), .a(decod_hexa_3_a), .b(decod_hexa_3_b), .e(decod_hexa_3_e),
    .d(decod_hexa_3_d), .c(decod_hexa_3_c), .dp(decod_hexa_3_dp));
endmodule

module meio_somador (
  input  A,
  input  B,
  output S,
  output C
);

  xor xor_1 (S, A, B);
  and and_1 (C, A, B);
endmodule

module somador_completo (
  input  Cin,
  input  A,
  input  B,
  output S,
  output Cout
);

  wire meio_somador_1_c, meio_somador_1_s, meio_somador_2_c;

  meio_somador meio_somador_1 (.A(A), .B(B), .C(meio_somador_1_c), .S(meio_somador_1_s));
  meio_somador meio_somador_2 (.A(meio_somador_1_s), .B(Cin), .C(meio_somador_2_c), .S(S));
  or or_1 (Cout, meio_somador_1_c, meio_somador_2_c);
endmodule

module somador_4bits (
  input  Cin,
  input  A0,
  input  A1,
  input  A2,
  input  A3,
  input  B0,
  input  B1,
  input  B2,
  input  B3,
  output S0,
  output S1,
  output S2,
  output S3,
  output Overflow,
  output Cout
);

  wire somador_completo_1_cout, somador_completo_2_cout, somador_completo_3_cout;

  somador_completo somador_completo_1 (.A(A0), .B(B0), .Cin(Cin), .Cout(somador_completo_1_cout), .S(S0));
  somador_completo somador_completo_2 (
    .A(A1), .B(B1), .Cin(somador_completo_1_cout), .Cout(somador_completo_2_cout), .S(S1));
  somador_completo somador_completo_3 (
    .A(A2), .B(B2), .Cin(somador_completo_2_cout), .Cout(somador_completo_3_cout), .S(S2));
  somador_completo somador_completo_4 (.A(A3), .B(B3), .Cin(somador_completo_3_cout), .Cout(Cout), .S(S3));
  xor xor_1 (Overflow, somador_completo_3_cout, Cout);
endmodule

module decod_hexa (
  input  E3,
  input  E2,
  input  E1,
  input  E0,
  output A,
  output B,
  output C,
  output D,
  output E,
  output F,
  output G,
  output DP
);

  wire and_1_out, and_2_out, and_3_out, and_4_out, and_5_out, and_6_out, and_7_out, and_8_out, and_9_out,
       and_10_out, and_11_out, and_12_out, and_13_out, and_14_out, and_15_out, and_16_out, and_17_out,
       and_18_out, and_19_out, and_20_out, and_21_out, and_22_out, and_23_out, and_24_out, and_25_out,
       and_26_out, and_27_out, and_28_out, and_29_out, and_30_out, and_31_out, and_32_out, and_33_out,
       and_34_out, and_35_out, not_1_out, not_2_out, not_3_out, not_4_out, not_5_out, not_6_out, not_7_out,
       not_8_out, not_9_out, not_10_out, not_11_out, not_12_out, not_13_out, not_14_out, not_15_out,
       not_16_out, not_17_out, not_18_out, not_19_out, not_20_out, not_21_out, not_22_out, not_23_out,
       not_24_out, not_25_out, not_26_out, not_27_out, not_28_out, not_29_out, not_30_out, not_31_out,
       not_32_out, not_33_out, not_34_out, not_35_out, not_36_out, not_37_out, not_38_out, not_39_out,
       not_40_out, not_41_out, not_42_out, not_43_out;

  not not_1 (not_1_out, E2);
  and and_1 (and_1_out, not_1_out, not_2_out);
  not not_2 (not_2_out, E0);
  not not_3 (not_3_out, E3);
  and and_2 (and_2_out, not_3_out, E1);
  not not_4 (not_4_out, E3);
  and and_3 (and_3_out, not_4_out, E2, E0);
  and and_4 (and_4_out, E2, E1);
  not not_5 (not_5_out, E2);
  and and_5 (and_5_out, E3, not_5_out, not_6_out);
  not not_6 (not_6_out, E1);
  and and_6 (and_6_out, E3, not_7_out);
  not not_7 (not_7_out, E0);
  not not_8 (not_8_out, E3);
  and and_7 (and_7_out, not_8_out, not_9_out);
  not not_9 (not_9_out, E2);
  not not_10 (not_10_out, E3);
  not not_11 (not_11_out, E1);
  and and_8 (and_8_out, not_10_out, not_11_out, not_12_out);
  not not_12 (not_12_out, E0);
  not not_13 (not_13_out, E2);
  and and_9 (and_9_out, not_13_out, not_14_out);
  not not_14 (not_14_out, E0);
  not not_15 (not_15_out, E3);
  and and_10 (and_10_out, not_15_out, E1, E0);
  and and_11 (and_11_out, E3, not_16_out, E0);
  not not_16 (not_16_out, E1);
  not not_17 (not_17_out, E3);
  and and_12 (and_12_out, not_17_out, not_18_out);
  not not_18 (not_18_out, E1);
  not not_19 (not_19_out, E3);
  and and_13 (and_13_out, not_19_out, E0);
  not not_20 (not_20_out, E1);
  and and_14 (and_14_out, not_20_out, E0);
  not not_21 (not_21_out, E3);
  and and_15 (and_15_out, not_21_out, E2);
  and and_16 (and_16_out, E3, not_22_out);
  not not_22 (not_22_out, E2);
  not not_23 (not_23_out, E3);
  not not_24 (not_24_out, E2);
  and and_17 (and_17_out, not_23_out, not_24_out, not_25_out);
  not not_25 (not_25_out, E0);
  not not_26 (not_26_out, E2);
  and and_18 (and_18_out, not_26_out, E1, E0);
  not not_27 (not_27_out, E1);
  and and_19 (and_19_out, E2, not_27_out, E0);
  and and_20 (and_20_out, E2, E1, not_28_out);
  not not_28 (not_28_out, E0);
  and and_21 (and_21_out, E3, not_29_out);
  not not_29 (not_29_out, E1);
  not not_30 (not_30_out, E2);
  and and_22 (and_22_out, not_30_out, not_31_out);
  not not_31 (not_31_out, E0);
  and and_23 (and_23_out, E1, not_32_out);
  not not_32 (not_32_out, E0);
  and and_24 (and_24_out, E3, E1);
  and and_25 (and_25_out, E3, E2);
  not not_33 (not_33_out, E2);
  and and_26 (and_26_out, not_33_out, E1);
  and and_27 (and_27_out, E1, not_34_out);
  not not_34 (not_34_out, E0);
  not not_35 (not_35_out, E3);
  and and_28 (and_28_out, not_35_out, E2, not_36_out);
  not not_36 (not_36_out, E1);
  and and_29 (and_29_out, E3, not_37_out);
  not not_37 (not_37_out, E2);
  and and_30 (and_30_out, E3, E0);
  not not_38 (not_38_out, E1);
  and and_31 (and_31_out, not_38_out, not_39_out);
  not not_39 (not_39_out, E0);
  not not_40 (not_40_out, E3);
  and and_32 (and_32_out, not_40_out, E2, not_41_out);
  not not_41 (not_41_out, E1);
  and and_33 (and_33_out, E2, not_42_out);
  not not_42 (not_42_out, E0);
  and and_34 (and_34_out, E3, not_43_out);
  not not_43 (not_43_out, E2);
  and and_35 (and_35_out, E3, E1);
  or or_1 (B, and_7_out, and_8_out, and_9_out, and_10_out, and_11_out);
  or or_2 (C, and_12_out, and_13_out, and_14_out, and_15_out, and_16_out);
  or or_3 (D, and_17_out, and_18_out, and_19_out, and_20_out, and_21_out);
  or or_4 (E, and_22_out, and_23_out, and_24_out, and_25_out);
  or or_5 (F, and_26_out, and_27_out, and_28_out, and_29_out, and_30_out);
  or or_6 (G, and_31_out, and_32_out, and_33_out, and_34_out, and_35_out);
  or or_7 (A, and_1_out, and_2_out, and_3_out, and_4_out, and_5_out, and_6_out);

  assign DP = 1'b0;
endmodule
