// Logisim project Projeto Sap-1 FINAL ATUALIZADO.circ as structural Verilog: 9 circuits, main circuit main
module main (
  input  CLR,
  output [3:0] HIGH,
  output [3:0] LOW,
  output Cout,
  output Out7,
  output Out6,
  output Out5,
  output Out4,
  output Out3,
  output Out2,
  output Out1,
  output Out0
);

  wire CLK_out, controlador_sequencializador_1_hlt, controlled_buffer_1_out, Cp, EA, Ep, EU, nCE, nEI, nL0,
       nLA, nLB, nLI, nLM, not_1_out, not_2_out, not_3_out, not_4_out, not_5_out, not_6_out, not_7_out,
       not_8_out, SU;
  wire [3:0] registrador_1_y0, registrador_1_y4, rem_1_y0;
  wire [7:0] bit_extender_1_out, registrador_2_y0, registrador_3_y0, ula_1_s, XOR_out;

  not not_1 (not_1_out, nLM);
  not not_2 (not_2_out, nCE);
  not not_3 (not_3_out, controlador_sequencializador_1_hlt);
  Contador_De_Programa contador_de_programa_1 (
    .C3(LOW[3]), .C2(LOW[2]), .C1(LOW[1]), .C0(LOW[0]), .COUNT(Cp), .CLR(CLR), .CLK(controlled_buffer_1_out),
    .ENABLE(Ep));
  REM rem_1 (
    .X3(LOW[3]), .X2(LOW[2]), .X1(LOW[1]), .X0(LOW[0]), .Y3(rem_1_y0[3]), .Y2(rem_1_y0[2]), .Y1(rem_1_y0[1]),
    .Y0(rem_1_y0[0]), .LOAD(not_1_out), .CLK(controlled_buffer_1_out), .CLR(CLR), .ENABLE(1'b1));
  RAM #(.addrWidth(4)) ram_1 (.addr(rem_1_y0), .data({HIGH, LOW}), .ld(not_2_out));  // open: sel, clk, clr
  Registrador registrador_1 (
    .X7(HIGH[3]), .X6(HIGH[2]), .X5(HIGH[1]), .X4(HIGH[0]), .X3(LOW[3]), .X2(LOW[2]), .X1(LOW[1]),
    .X0(LOW[0]), .Y7(registrador_1_y4[3]), .Y6(registrador_1_y4[2]), .Y5(registrador_1_y4[1]),
    .Y4(registrador_1_y4[0]), .Y3(registrador_1_y0[3]), .Y2(registrador_1_y0[2]), .Y1(registrador_1_y0[1]),
    .Y0(registrador_1_y0[0]), .LOAD(not_4_out), .CLK(controlled_buffer_1_out), .CLR(CLR), .ENABLE(1'b1));
  Controlador___Sequencializador controlador_sequencializador_1 (
    .I7_I6_I5_I4(registrador_1_y4), .HLT(controlador_sequencializador_1_hlt), .Cp(Cp), .Ep(Ep), .nLM(nLM),
    .nCE(nCE), .nLi(nLI), .nEI(nEI), .nLA(nLA), .EA(EA), .SU(SU), .EU(EU), .nLB(nLB), .nL0(nL0),
    .CLK(controlled_buffer_1_out), .CLR(CLR));
  Clock CLK (.out(CLK_out));
  assign controlled_buffer_1_out = not_3_out ? CLK_out : 1'bz;  // Controlled_Buffer controlled_buffer_1
  not not_4 (not_4_out, nLI);
  assign LOW = not_5_out ? registrador_1_y0 : 4'bz;  // Controlled_Buffer controlled_buffer_2
  not not_5 (not_5_out, nEI);
  not not_6 (not_6_out, nLA);
  Registrador registrador_2 (
    .X7(HIGH[3]), .X6(HIGH[2]), .X5(HIGH[1]), .X4(HIGH[0]), .X3(LOW[3]), .X2(LOW[2]), .X1(LOW[1]),
    .X0(LOW[0]), .Y7(registrador_2_y0[7]), .Y6(registrador_2_y0[6]), .Y5(registrador_2_y0[5]),
    .Y4(registrador_2_y0[4]), .Y3(registrador_2_y0[3]), .Y2(registrador_2_y0[2]), .Y1(registrador_2_y0[1]),
    .Y0(registrador_2_y0[0]), .LOAD(not_6_out), .CLK(controlled_buffer_1_out), .CLR(CLR), .ENABLE(1'b1));
  assign {HIGH, LOW} = EA ? registrador_2_y0 : 8'bz;  // Controlled_Buffer controlled_buffer_3
  assign {HIGH, LOW} = EU ? ula_1_s : 8'bz;  // Controlled_Buffer controlled_buffer_4
  not not_7 (not_7_out, nLB);
  not not_8 (not_8_out, nL0);
  ULA ula_1 (.X(registrador_2_y0), .Y(XOR_out), .Cin(SU), .S(ula_1_s), .Cout(Cout));
  Registrador registrador_3 (
    .X7(HIGH[3]), .X6(HIGH[2]), .X5(HIGH[1]), .X4(HIGH[0]), .X3(LOW[3]), .X2(LOW[2]), .X1(LOW[1]),
    .X0(LOW[0]), .Y7(registrador_3_y0[7]), .Y6(registrador_3_y0[6]), .Y5(registrador_3_y0[5]),
    .Y4(registrador_3_y0[4]), .Y3(registrador_3_y0[3]), .Y2(registrador_3_y0[2]), .Y1(registrador_3_y0[1]),
    .Y0(registrador_3_y0[0]), .LOAD(not_7_out), .CLK(controlled_buffer_1_out), .CLR(CLR), .ENABLE(1'b1));
  Registrador registrador_4 (
    .X7(HIGH[3]), .X6(HIGH[2]), .X5(HIGH[1]), .X4(HIGH[0]), .X3(LOW[3]), .X2(LOW[2]), .X1(LOW[1]),
    .X0(LOW[0]), .Y7(Out7), .Y6(Out6), .Y5(Out5), .Y4(Out4), .Y3(Out3), .Y2(Out2), .Y1(Out1), .Y0(Out0),
    .LOAD(not_8_out), .CLK(controlled_buffer_1_out), .CLR(CLR), .ENABLE(1'b1));
  assign XOR_out = registrador_3_y0 ^ bit_extender_1_out;  // XOR_Gate XOR, 8 bits wide
  assign bit_extender_1_out = {{7{SU}}, SU};  // Bit_Extender bit_extender_1
  Hex_Digit_Display hex_digit_display_1 (.value({Out7, Out6, Out5, Out4}));  // open: dp
  Hex_Digit_Display hex_digit_display_2 (.value({Out3, Out2, Out1, Out0}));  // open: dp

  // Notes on the sheet:
  //   Resultado:
  //   66 - 24 = 42
  //   42 + 07 = 49
  //   49 - 40 = 09
  //   Vídeo Explicativo:
  //   https://youtu.be/z5WwWpGWlGs
  //   Integrantes:
  //   Caio Gomes Alcântara Glória
  //   Daniel Salgado Magalhães
  //   Gabriel Henrique Vieira de Oliveira
  //   Instrução para RAM:
  //   09 e0 2a e0 1b e0 2c e0 f0 66 24 07 40 00 00 00
  //   ENABLE
  //   ADD/SUB
  //   A
  //   B
  //   OUT
endmodule

// CB
module \Contador_de_Binário  (
  input  X,
  input  Y,
  input  Z,
  output S,
  output C
);

  wire AND_1_out, AND_2_out, XOR_1_out;

  xor XOR_1 (XOR_1_out, X, Y);
  and AND_1 (AND_1_out, X, Y);
  xor XOR_2 (S, XOR_1_out, Z);
  and AND_2 (AND_2_out, Z, XOR_1_out);
  or OR (C, AND_2_out, AND_1_out);
endmodule

module REM (
  input  X3,
  input  X2,
  input  X1,
  input  X0,
  input  LOAD,
  input  CLK,
  input  CLR,
  input  ENABLE,
  output Y3,
  output Y2,
  output Y1,
  output Y0
);

  wire and_1_out, and_2_out, and_3_out, and_4_out, and_5_out, and_6_out, and_7_out, and_8_out, d_ff_1_q,
       d_ff_2_q, d_ff_3_q, d_ff_4_q, not_1_out, or_1_out, or_2_out, or_3_out, or_4_out;

  and and_1 (and_1_out, X3, LOAD);
  and and_2 (and_2_out, d_ff_1_q, not_1_out);
  or or_1 (or_1_out, and_2_out, and_1_out);
  D_Flip_Flop d_ff_1 (.clk(CLK), .D(or_1_out), .Q(d_ff_1_q), .reset(CLR));  // open: Qn, preset, en
  assign Y3 = ENABLE ? d_ff_1_q : 1'bz;  // Controlled_Buffer controlled_buffer_1
  and and_3 (and_3_out, d_ff_2_q, not_1_out);
  or or_2 (or_2_out, and_3_out, and_4_out);
  and and_4 (and_4_out, X2, LOAD);
  D_Flip_Flop d_ff_2 (.clk(CLK), .D(or_2_out), .Q(d_ff_2_q), .reset(CLR));  // open: Qn, preset, en
  assign Y2 = ENABLE ? d_ff_2_q : 1'bz;  // Controlled_Buffer controlled_buffer_2
  and and_5 (and_5_out, d_ff_3_q, not_1_out);
  or or_3 (or_3_out, and_5_out, and_6_out);
  and and_6 (and_6_out, X1, LOAD);
  D_Flip_Flop d_ff_3 (.clk(CLK), .D(or_3_out), .Q(d_ff_3_q), .reset(CLR));  // open: Qn, preset, en
  and and_7 (and_7_out, d_ff_4_q, not_1_out);
  assign Y1 = ENABLE ? d_ff_3_q : 1'bz;  // Controlled_Buffer controlled_buffer_3
  not not_1 (not_1_out, LOAD);
  and and_8 (and_8_out, X0, LOAD);
  or or_4 (or_4_out, and_7_out, and_8_out);
  D_Flip_Flop d_ff_4 (.clk(CLK), .D(or_4_out), .Q(d_ff_4_q), .reset(CLR));  // open: Qn, preset, en
  assign Y0 = ENABLE ? d_ff_4_q : 1'bz;  // Controlled_Buffer controlled_buffer_4
endmodule

module Registrador (
  input  X3,
  input  X2,
  input  X1,
  input  X0,
  input  X7,
  input  X6,
  input  X5,
  input  X4,
  input  LOAD,
  input  CLK,
  input  CLR,
  input  ENABLE,
  output Y3,
  output Y2,
  output Y1,
  output Y0,
  output Y5,
  output Y4,
  output Y7,
  output Y6
);

  wire and_1_out, and_2_out, and_3_out, and_4_out, and_5_out, and_6_out, and_7_out, and_8_out, and_9_out,
       and_10_out, and_11_out, and_12_out, and_13_out, and_14_out, and_15_out, and_16_out, d_ff_1_q,
       d_ff_2_q, d_ff_3_q, d_ff_4_q, d_ff_5_q, d_ff_6_q, d_ff_7_q, d_ff_8_q, not_1_out, or_1_out, or_2_out,
       or_3_out, or_4_out, or_5_out, or_6_out, or_7_out, or_8_out;

  and and_1 (and_1_out, X7, LOAD);
  and and_2 (and_2_out, d_ff_1_q, not_1_out);
  or or_1 (or_1_out, and_2_out, and_1_out);
  D_Flip_Flop d_ff_1 (.clk(CLK), .D(or_1_out), .Q(d_ff_1_q), .reset(CLR));  // open: Qn, preset, en
  assign Y7 = ENABLE ? d_ff_1_q : 1'bz;  // Controlled_Buffer controlled_buffer_1
  and and_3 (and_3_out, d_ff_2_q, not_1_out);
  or or_2 (or_2_out, and_3_out, and_4_out);
  and and_4 (and_4_out, X6, LOAD);
  D_Flip_Flop d_ff_2 (.clk(CLK), .D(or_2_out), .Q(d_ff_2_q), .reset(CLR));  // open: Qn, preset, en
  assign Y6 = ENABLE ? d_ff_2_q : 1'bz;  // Controlled_Buffer controlled_buffer_2
  and and_5 (and_5_out, d_ff_3_q, not_1_out);
  or or_3 (or_3_out, and_5_out, and_6_out);
  and and_6 (and_6_out, X5, LOAD);
  D_Flip_Flop d_ff_3 (.clk(CLK), .D(or_3_out), .Q(d_ff_3_q), .reset(CLR));  // open: Qn, preset, en
  and and_7 (and_7_out, d_ff_4_q, not_1_out);
  assign Y5 = ENABLE ? d_ff_3_q : 1'bz;  // Controlled_Buffer controlled_buffer_3
  and and_8 (and_8_out, X4, LOAD);
  or or_4 (or_4_out, and_7_out, and_8_out);
  D_Flip_Flop d_ff_4 (.clk(CLK), .D(or_4_out), .Q(d_ff_4_q), .reset(CLR));  // open: Qn, preset, en
  assign Y4 = ENABLE ? d_ff_4_q : 1'bz;  // Controlled_Buffer controlled_buffer_4
  and and_9 (and_9_out, d_ff_5_q, not_1_out);
  or or_5 (or_5_out, and_9_out, and_10_out);
  and and_10 (and_10_out, X3, LOAD);
  D_Flip_Flop d_ff_5 (.clk(CLK), .D(or_5_out), .Q(d_ff_5_q), .reset(CLR));  // open: Qn, preset, en
  assign Y3 = ENABLE ? d_ff_5_q : 1'bz;  // Controlled_Buffer controlled_buffer_5
  and and_11 (and_11_out, d_ff_6_q, not_1_out);
  or or_6 (or_6_out, and_11_out, and_12_out);
  and and_12 (and_12_out, X2, LOAD);
  D_Flip_Flop d_ff_6 (.clk(CLK), .D(or_6_out), .Q(d_ff_6_q), .reset(CLR));  // open: Qn, preset, en
  and and_13 (and_13_out, d_ff_7_q, not_1_out);
  assign Y2 = ENABLE ? d_ff_6_q : 1'bz;  // Controlled_Buffer controlled_buffer_6
  and and_14 (and_14_out, X1, LOAD);
  or or_7 (or_7_out, and_13_out, and_14_out);
  D_Flip_Flop d_ff_7 (.clk(CLK), .D(or_7_out), .Q(d_ff_7_q), .reset(CLR));  // open: Qn, preset, en
  and and_15 (and_15_out, d_ff_8_q, not_1_out);
  assign Y1 = ENABLE ? d_ff_7_q : 1'bz;  // Controlled_Buffer controlled_buffer_7
  not not_1 (not_1_out, LOAD);
  and and_16 (and_16_out, X0, LOAD);
  or or_8 (or_8_out, and_15_out, and_16_out);
  D_Flip_Flop d_ff_8 (.clk(CLK), .D(or_8_out), .Q(d_ff_8_q), .reset(CLR));  // open: Qn, preset, en
  assign Y0 = ENABLE ? d_ff_8_q : 1'bz;  // Controlled_Buffer controlled_buffer_8
endmodule

module ULA (
  input  [7:0] X,
  input  [7:0] Y,
  input  Cin,
  output [7:0] S,
  output Cout
);

  wire \contador_de_binário_1_c , \contador_de_binário_2_c , \contador_de_binário_3_c ,
       \contador_de_binário_4_c , \contador_de_binário_5_c , \contador_de_binário_6_c ,
       \contador_de_binário_7_c ;

  \Contador_de_Binário  \contador_de_binário_1  (.X(X[0]), .Y(Y[0]), .Z(Cin), .S(S[0]), .C(\contador_de_binário_1_c ));
  \Contador_de_Binário  \contador_de_binário_2  (
    .X(X[1]), .Y(Y[1]), .Z(\contador_de_binário_1_c ), .S(S[1]), .C(\contador_de_binário_2_c ));
  \Contador_de_Binário  \contador_de_binário_3  (
    .X(X[2]), .Y(Y[2]), .Z(\contador_de_binário_2_c ), .S(S[2]), .C(\contador_de_binário_3_c ));
  \Contador_de_Binário  \contador_de_binário_4  (
    .X(X[3]), .Y(Y[3]), .Z(\contador_de_binário_3_c ), .S(S[3]), .C(\contador_de_binário_4_c ));
  \Contador_de_Binário  \contador_de_binário_5  (
    .X(X[4]), .Y(Y[4]), .Z(\contador_de_binário_4_c ), .S(S[4]), .C(\contador_de_binário_5_c ));
  \Contador_de_Binário  \contador_de_binário_6  (
    .X(X[5]), .Y(Y[5]), .Z(\contador_de_binário_5_c ), .S(S[5]), .C(\contador_de_binário_6_c ));
  \Contador_de_Binário  \contador_de_binário_7  (
    .X(X[6]), .Y(Y[6]), .Z(\contador_de_binário_6_c ), .S(S[6]), .C(\contador_de_binário_7_c ));
  \Contador_de_Binário  \contador_de_binário_8  (.X(X[7]), .Y(Y[7]), .Z(\contador_de_binário_7_c ), .S(S[7]), .C(Cout));

  // Notes on the sheet:
  //   X=4 (00000100)
  //   Y=8 (00001000)
endmodule

// PC
module Contador_De_Programa (
  input  COUNT,
  input  CLR,
  input  CLK,
  input  ENABLE,
  output C3,
  output C2,
  output C1,
  output C0
);

  wire AND1_out, AND2_out, AND3_out, j_k_ff_1_q, j_k_ff_2_q, j_k_ff_3_q, j_k_ff_4_q;

  and AND3 (AND3_out, COUNT, AND2_out, j_k_ff_2_q);
  J_K_Flip_Flop j_k_ff_1 (.J(AND3_out), .clk(CLK), .K(AND3_out), .Q(j_k_ff_1_q), .reset(CLR));  // open: Qn, preset, en
  assign C3 = ENABLE ? j_k_ff_1_q : 1'bz;  // Controlled_Buffer controlled_buffer_1
  and AND2 (AND2_out, COUNT, AND1_out, j_k_ff_3_q);
  J_K_Flip_Flop j_k_ff_2 (.J(AND2_out), .clk(CLK), .K(AND2_out), .Q(j_k_ff_2_q), .reset(CLR));  // open: Qn, preset, en
  assign C2 = ENABLE ? j_k_ff_2_q : 1'bz;  // Controlled_Buffer controlled_buffer_2
  and AND1 (AND1_out, COUNT, j_k_ff_4_q);
  J_K_Flip_Flop j_k_ff_3 (.J(AND1_out), .clk(CLK), .K(AND1_out), .Q(j_k_ff_3_q), .reset(CLR));  // open: Qn, preset, en
  assign C1 = ENABLE ? j_k_ff_3_q : 1'bz;  // Controlled_Buffer controlled_buffer_3
  J_K_Flip_Flop j_k_ff_4 (.J(COUNT), .clk(CLK), .K(COUNT), .Q(j_k_ff_4_q), .reset(CLR));  // open: Qn, preset, en
  assign C0 = ENABLE ? j_k_ff_4_q : 1'bz;  // Controlled_Buffer controlled_buffer_4

  // Notes on the sheet:
  //   Ripple Counter
  //   Program Counter
endmodule

// CA
module Contador_em_Anel (
  input  CLK,
  input  CLR,
  output T6,
  output T5,
  output T4,
  output T3,
  output T2,
  output T1
);

  wire j_k_ff_1_qn, j_k_ff_2_qn, j_k_ff_3_qn, j_k_ff_4_qn, j_k_ff_5_qn, j_k_ff_6_q;

  J_K_Flip_Flop j_k_ff_1 (
    .J(T5), .clk(CLK), .K(j_k_ff_2_qn), .Q(T6), .Qn(j_k_ff_1_qn), .reset(CLR));  // open: preset, en
  J_K_Flip_Flop j_k_ff_2 (
    .J(T4), .clk(CLK), .K(j_k_ff_3_qn), .Q(T5), .Qn(j_k_ff_2_qn), .reset(CLR));  // open: preset, en
  J_K_Flip_Flop j_k_ff_3 (
    .J(T3), .clk(CLK), .K(j_k_ff_4_qn), .Q(T4), .Qn(j_k_ff_3_qn), .reset(CLR));  // open: preset, en
  J_K_Flip_Flop j_k_ff_4 (
    .J(T2), .clk(CLK), .K(j_k_ff_5_qn), .Q(T3), .Qn(j_k_ff_4_qn), .reset(CLR));  // open: preset, en
  J_K_Flip_Flop j_k_ff_5 (
    .J(T1), .clk(CLK), .K(j_k_ff_6_q), .Q(T2), .Qn(j_k_ff_5_qn), .reset(CLR));  // open: preset, en
  J_K_Flip_Flop j_k_ff_6 (
    .J(j_k_ff_1_qn), .clk(CLK), .K(T6), .Q(j_k_ff_6_q), .Qn(T1), .reset(CLR));  // open: preset, en
endmodule

// Decoder
module Decodificador (
  input  I7,
  input  I6,
  input  I5,
  input  I4,
  output LDA,
  output ADD,
  output SUB,
  output OUT,
  output HALT
);

  wire and_1_out, and_2_out, and_3_out, and_4_out, and_5_out, not_1_out, not_2_out, not_3_out, not_4_out;

  not not_1 (not_1_out, I7);
  not not_2 (not_2_out, I6);
  not not_3 (not_3_out, I5);
  not not_4 (not_4_out, I4);
  and and_1 (and_1_out, not_1_out, not_2_out, not_3_out, not_4_out);
  and and_2 (and_2_out, not_1_out, not_2_out, not_3_out, I4);
  and and_3 (and_3_out, not_1_out, not_2_out, I5, not_4_out);
  and and_4 (and_4_out, I7, I6, I5, not_4_out);
  and and_5 (and_5_out, I7, I6, I5, I4);
  buf buffer_1 (LDA, and_1_out);
  buf buffer_2 (ADD, and_2_out);
  buf buffer_3 (SUB, and_3_out);
  buf buffer_4 (OUT, and_4_out);
  buf buffer_5 (HALT, and_5_out);
endmodule

// C/S
module Controlador___Sequencializador (
  input  CLK,
  input  CLR,
  input  [3:0] I7_I6_I5_I4,
  output nLM,
  output nCE,
  output nLi,
  output nEI,
  output nLA,
  output EA,
  output SU,
  output EU,
  output nLB,
  output nL0,
  output HLT,
  output Cp,
  output Ep
);

  wire and_1_out, and_2_out, and_3_out, and_4_out, and_5_out, and_6_out, and_7_out, and_8_out, and_9_out,
       and_10_out, and_11_out, and_12_out, and_14_out, and_16_out, and_17_out, and_18_out, and_19_out,
       contador_em_anel_1_t3, contador_em_anel_1_t4, contador_em_anel_1_t5, contador_em_anel_1_t6,
       decodificador_1_add, decodificador_1_lda, decodificador_1_out, decodificador_1_sub, or_1_out,
       or_2_out, or_3_out, or_4_out, or_6_out;

  Decodificador decodificador_1 (
    .I7(I7_I6_I5_I4[3]), .I6(I7_I6_I5_I4[2]), .I5(I7_I6_I5_I4[1]), .I4(I7_I6_I5_I4[0]),
    .LDA(decodificador_1_lda), .ADD(decodificador_1_add), .SUB(decodificador_1_sub),
    .OUT(decodificador_1_out), .HALT(HLT));
  and and_1 (and_1_out, decodificador_1_lda, contador_em_anel_1_t4);
  and and_2 (and_2_out, decodificador_1_add, contador_em_anel_1_t4);
  and and_3 (and_3_out, decodificador_1_sub, contador_em_anel_1_t4);
  or or_1 (or_1_out, Ep, and_1_out, and_2_out, and_3_out);
  not not_1 (nLM, or_1_out);
  and and_4 (and_4_out, decodificador_1_lda, contador_em_anel_1_t5);
  and and_5 (and_5_out, decodificador_1_add, contador_em_anel_1_t5);
  and and_6 (and_6_out, decodificador_1_sub, contador_em_anel_1_t5);
  or or_2 (or_2_out, contador_em_anel_1_t3, and_4_out, and_5_out, and_6_out);
  not not_2 (nCE, or_2_out);
  Contador_em_Anel contador_em_anel_1 (
    .T6(contador_em_anel_1_t6), .T5(contador_em_anel_1_t5), .T4(contador_em_anel_1_t4),
    .T3(contador_em_anel_1_t3), .T2(Cp), .T1(Ep), .CLK(CLK), .CLR(CLR));
  not not_3 (nLi, contador_em_anel_1_t3);
  and and_7 (and_7_out, decodificador_1_lda, contador_em_anel_1_t4);
  and and_8 (and_8_out, decodificador_1_add, contador_em_anel_1_t4);
  and and_9 (and_9_out, decodificador_1_sub, contador_em_anel_1_t4);
  or or_3 (or_3_out, and_7_out, and_8_out, and_9_out);
  not not_4 (nEI, or_3_out);
  and and_10 (and_10_out, decodificador_1_lda, contador_em_anel_1_t5);
  and and_11 (and_11_out, decodificador_1_add, contador_em_anel_1_t6);
  and and_12 (and_12_out, decodificador_1_sub, contador_em_anel_1_t6);
  or or_4 (or_4_out, and_10_out, and_11_out, and_12_out);
  not not_5 (nLA, or_4_out);
  and and_13 (EA, decodificador_1_out, contador_em_anel_1_t4);
  and and_14 (and_14_out, decodificador_1_add, contador_em_anel_1_t6);
  and and_15 (SU, decodificador_1_sub, contador_em_anel_1_t6);
  and and_16 (and_16_out, decodificador_1_sub, contador_em_anel_1_t6);
  or or_5 (EU, and_14_out, and_16_out);
  and and_17 (and_17_out, decodificador_1_add, contador_em_anel_1_t5);
  and and_18 (and_18_out, decodificador_1_sub, contador_em_anel_1_t5);
  or or_6 (or_6_out, and_17_out, and_18_out);
  not not_6 (nLB, or_6_out);
  and and_19 (and_19_out, decodificador_1_out, contador_em_anel_1_t4);
  not not_7 (nL0, and_19_out);
endmodule
