// Logisim project ULA_arq2.circ as structural Verilog: 6 circuits, main circuit ULA 4bits
module ULA_4bits (
  input  A3,
  input  A2,
  input  A1,
  input  A0,
  input  B3,
  input  B2,
  input  B1,
  input  B0,
  input  Op2,
  input  Op1,
  input  Binvert,
  output S0,
  output S1,
  output S2,
  output S3,
  output Cout
);

  wire ula1bit_1_cout, ula1bit_2_cout, ula1bit_3_cout;

  ULA1bit ula1bit_1 (
    .A(A0), .B(B0), .Binvert(Binvert), .Cin(Binvert), .Op1(Op2), .Op0(Op1), .Cout(ula1bit_1_cout), .S(S0));
  ULA1bit ula1bit_2 (
    .A(A1), .B(B1), .Binvert(Binvert), .Cin(ula1bit_1_cout), .Op1(Op2), .Op0(Op1), .Cout(ula1bit_2_cout),
    .S(S1));
  ULA1bit ula1bit_3 (
    .A(A2), .B(B2), .Binvert(Binvert), .Cin(ula1bit_2_cout), .Op1(Op2), .Op0(Op1), .Cout(ula1bit_3_cout),
    .S(S2));
  ULA1bit ula1bit_4 (
    .A(A3), .B(B3), .Binvert(Binvert), .Cin(ula1bit_3_cout), .Op1(Op2), .Op0(Op1), .Cout(Cout), .S(S3));

  // Notes on the sheet:
  //   Arthur Martinho - 813168$Daniel Salgado - 821429
endmodule

module _4bitsMUX (
  input  Op1,
  input  Op2,
  input  E0,
  input  E1,
  input  E2,
  input  E3,
  output S
);

  wire and_1_out, and_2_out, and_3_out, and_4_out, not_1_out, not_2_out, not_3_out, not_4_out;

  not not_1 (not_1_out, Op1);
  not not_2 (not_2_out, Op1);
  and and_1 (and_1_out, E0, not_1_out, not_3_out);
  not not_3 (not_3_out, Op2);
  and and_2 (and_2_out, E1, not_2_out, Op2);
  and and_3 (and_3_out, E2, Op1, not_4_out);
  not not_4 (not_4_out, Op2);
  and and_4 (and_4_out, E3, Op1, Op2);
  or or_1 (S, and_1_out, and_2_out, and_3_out, and_4_out);
endmodule

module _2bitsMUX (
  input  Op1,
  input  E0,
  input  E1,
  output S
);

  wire and_1_out, and_2_out, not_1_out;

  not not_1 (not_1_out, Op1);
  and and_1 (and_1_out, E0, not_1_out);
  and and_2 (and_2_out, E1, Op1);
  or or_1 (S, and_1_out, and_2_out);
endmodule

module meio_somador (
  input  in_1,
  input  in_2,
  output out_3,
  output out_4
);

  xor xor_1 (out_3, in_1, in_2);
  and and_1 (out_4, in_1, in_2);
endmodule

module somador_completo (
  input  in_1,
  input  in_2,
  input  in_3,
  output out_4,
  output out_5
);

  wire meio_somador_1_out_3, meio_somador_1_out_4, meio_somador_2_out_4;

  meio_somador meio_somador_1 (.in_1(in_1), .in_2(in_3), .out_4(meio_somador_1_out_4), .out_3(meio_somador_1_out_3));
  meio_somador meio_somador_2 (.in_1(meio_somador_1_out_3), .in_2(in_2), .out_4(meio_somador_2_out_4), .out_3(out_4));
  or or_1 (out_5, meio_somador_2_out_4, meio_somador_1_out_4);
endmodule

module ULA1bit (
  input  Binvert,
  input  Cin,
  input  Op1,
  input  Op0,
  input  A,
  input  B,
  output S,
  output Cout
);

  wire and_1_out, n2bitsmux_1_s, not_1_out, not_2_out, or_1_out, somador_completo_1_out_4;

  not not_1 (not_1_out, B);
  _2bitsMUX u_2bitsmux_1 (.E0(B), .E1(not_1_out), .Op1(Binvert), .S(n2bitsmux_1_s));
  and and_1 (and_1_out, A, n2bitsmux_1_s);
  or or_1 (or_1_out, A, n2bitsmux_1_s);
  not not_2 (not_2_out, A);
  somador_completo somador_completo_1 (
    .in_1(A), .in_3(n2bitsmux_1_s), .in_2(Cin), .out_5(Cout), .out_4(somador_completo_1_out_4));
  _4bitsMUX u_4bitsmux_1 (
    .E0(and_1_out), .E1(or_1_out), .E2(not_2_out), .E3(somador_completo_1_out_4), .Op1(Op1), .Op2(Op0), .S(S));

  // Notes on the sheet:
  //   Arthur Martinho - 813168$Daniel Salgado - 821429
endmodule
